# Fritzing sketch IR2DMX (saved by Fritzing 0.9.3b)
breadboards: 3

parts:
  DMX_Out = XLR3_NCFAH2 [package=xlr3_nc3fah2]
  P3 = S1133 Si Photodiode [package="8mm Ceramic [THT]"]
  R9 = Resistor [tolerance=±5% resistance=10k package=THT]
  Slider = SLIDER [package=slider]
  Power_In = XLR3_NCFAH2 [package=xlr3_nc3fah2]
  S5 = Round Pushbutton
  LCD1 = LCD screen
  U7 = SLIDER [package=slider]
  S1 = Round Pushbutton
  U4 = SLIDER [package=slider]
  part = Resistor [tolerance=±5% resistance=10k package=THT]
  P1 = S1133 Si Photodiode [package="8mm Ceramic [THT]"]
  Part1 = Arduino Nano (Rev3.0)
  R6 = Resistor [tolerance=±5% resistance=10k package=THT]
  U8 = SLIDER [package=slider]
  part_2 = Resistor [tolerance=±5% resistance=220 package=THT]
  part_3 = Resistor [tolerance=±5% resistance=22 package=THT]
  U5 = SLIDER [package=slider]
  part_4 = Resistor [tolerance=±5% resistance=10k package=THT]
  Buttons = Round Pushbutton
  P2 = S1133 Si Photodiode [package="8mm Ceramic [THT]"]
  S4 = Round Pushbutton
  part_5 = Resistor [tolerance=±5% resistance=22 package=THT]
  part_6 = Resistor [tolerance=±5% resistance=120 package=THT]
  R7 = Resistor [tolerance=±5% resistance=10k package=THT]
  IR_Photodiodes = S1133 Si Photodiode [package="8mm Ceramic [THT]"]
  LCD_Contrast = POT [package=pot_mammoth]
  part_7 = SN75176A [part_number=SN75176 package=dil08]
  U3 = SLIDER [package=slider]

nets:
  GND: DMX_Out.1, P3.cathode, R9.Pin_0, Slider.A, Power_In.1, LCD1.VSS, LCD1.R/W, LCD1.LED-, U7.A, U4.A, part.Pin_0, P1.cathode, Part1.GND, R6.Pin_1, U8.A, U5.A, part_4.Pin_1, P2.cathode, R7.Pin_0, IR_Photodiodes.cathode, LCD_Contrast.E, part_7.GND, U3.A
  N1: DMX_Out.2, part_5.Pin_0, part_6.Pin_0
  N2: DMX_Out.3, part_3.Pin_0, part_6.Pin_1
  N3: P3.anode, part.Pin_1, P1.anode, Part1.A0, P2.anode, IR_Photodiodes.anode
  N4: R9.Pin_1, S5.leg1, Part1.D9
  5V: Slider.E, Power_In.2, S5.leg0, LCD1.VDD, U7.E, S1.leg0, U4.E, Part1.VIN, U8.E, part_2.Pin_0, U5.E, Buttons.leg1, S4.leg1, LCD_Contrast.A, part_7.¬RE, part_7.DE, part_7.VCC, U3.E
  N5: Slider.S, Part1.A1
  N6: LCD1.V0, LCD_Contrast.S
  N7: LCD1.RS, Part1.D12/MISO
  N8: LCD1.E, Part1.D11/MOSI
  N9: LCD1.DB4, Part1.D5
  N10: LCD1.DB5, Part1.D4
  N11: LCD1.DB6, Part1.D3
  N12: LCD1.DB7, Part1.D2
  N13: LCD1.LED+, part_2.Pin_1
  N14: U7.S, Part1.A2
  N15: S1.leg1, Part1.D8, R6.Pin_0
  N16: U4.S, Part1.A5
  N17: Part1.D6, part_7.D
  N18: Part1.D7, part_4.Pin_0, Buttons.leg0
  N19: Part1.D10, S4.leg0, R7.Pin_1
  N20: Part1.A6, U3.S
  N21: Part1.A4, U5.S
  N22: Part1.A3, U8.S
  N23: part_3.Pin_1, part_7.A
  N24: part_5.Pin_1, part_7.B

custom parts:
  SN75176A: RS-485 transceiver
